# Fritzing sketch Arduino GPS (saved by Fritzing 0.9.10b)

parts:
  OLED_I2C1 = OLED 128x64 I2C Monochrome Display
  A1 = NEO-6M GPS Module [part_number=GY-GPS6MV2]
  Componente1 = Arduino Uno (Rev3)-TopMount

nets:
  N1: OLED_I2C1.SDA, Componente1.A4/SDA
  N2: OLED_I2C1.SCK, Componente1.A5/SCL
  GND: OLED_I2C1.GND, A1.GND, Componente1.GND
  N3: A1.Tx, Componente1.D2
  VCC: A1.Vcc, Componente1.5V

custom parts:
  NEO-6M GPS Module: GY-GPS6MV2 NEO-6M GPS Module Module based on U-blox NEO-6M GPS engine, incorporating regulator for 3.3-5V DC input, MS621FE-compatible rechargeable battery for backup and EEPROM for storing configuration settings. Links: NEO-6 series product information page NEO-6 Datasheet
  Arduino Uno (Rev3)-TopMount: Arduino Uno (Rev3) for Top PCB Mount. The PCB view of the Arduino Uno (Rev3) in Arduino Bin flipped upside down with the text flipped back so as to be readable. Other views haven't changed Protruding component position is outlined to provide indication of part contact. Number in component outline is mm of protrusion of the component from the UNO PCB. Subtract the number from the USB (11mm),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
